// Logisim project HW 2.circ as structural Verilog: 1 circuit, main circuit main
module main (
  input  X,
  input  X_2,
  input  X_3,
  input  Y,
  input  X_4,
  input  Y_2,
  input  X_5,
  input  Y_3,
  input  X_6,
  input  Y_4,
  output X_prime,
  output X_prime_2,
  output XY,
  output XY_2,
  output X_Y,
  output X_Y_2
);

  wire nand_2_out, nand_3_out, nand_4_out, nor_2_out, nor_3_out, nor_4_out;

  nand nand_1 (X_prime, X, X);
  nor nor_1 (X_prime_2, X_2, X_2);
  nand nand_2 (nand_2_out, X_3, Y);
  nor nor_2 (nor_2_out, X_4, X_4);
  nor nor_3 (nor_3_out, Y_2, Y_2);
  nor nor_4 (nor_4_out, X_5, Y_3);
  nand nand_3 (nand_3_out, X_6, X_6);
  nand nand_4 (nand_4_out, Y_4, Y_4);
  nand nand_5 (XY, nand_2_out, nand_2_out);
  nor nor_5 (XY_2, nor_2_out, nor_3_out);
  nor nor_6 (X_Y, nor_4_out, nor_4_out);
  nand nand_6 (X_Y_2, nand_3_out, nand_4_out);

  // Notes on the sheet:
  //   NOT Gates
  //   AND Gates
  //   OR gates
endmodule
