// Logisim project 4BitCounter.circ as structural Verilog: 1 circuit, main circuit main
module main (
  input  in_1,
  output out_2,
  output out_3,
  output out_4,
  output out_5
);

  wire and_1_out, and_2_out, and_3_out;

  and and_1 (and_1_out, and_3_out, out_3);
  and and_2 (and_2_out, and_1_out, out_4);
  and and_3 (and_3_out, 1'b1, out_2);
  J_K_Flip_Flop j_k_ff_1 (.J(1'b1), .clk(in_1), .K(1'b1), .Q(out_2));  // open: Qn, preset, en, reset
  J_K_Flip_Flop j_k_ff_2 (.J(and_3_out), .clk(in_1), .K(and_3_out), .Q(out_3));  // open: Qn, preset, en, reset
  J_K_Flip_Flop j_k_ff_3 (.J(and_1_out), .clk(in_1), .K(and_1_out), .Q(out_4));  // open: Qn, preset, en, reset
  J_K_Flip_Flop j_k_ff_4 (.J(and_2_out), .clk(in_1), .K(and_2_out), .Q(out_5));  // open: Qn, preset, en, reset
endmodule
