// Logisim project Counter2.circ as structural Verilog: 2 circuits, main circuit main
module main (
);

  wire and_1_out, and_2_out, and_3_out, and_4_out, and_5_out, button_1_out, j_k_ff_1_q, j_k_ff_2_q,
       not_1_out, not_2_out, or_1_out, or_2_out, or_3_out, or_4_out, or_5_out;

  Button button_1 (.out(button_1_out));
  and and_1 (and_1_out, 1'b1, j_k_ff_1_q);
  J_K_Flip_Flop j_k_ff_1 (.J(1'b1), .clk(button_1_out), .K(1'b1), .Q(j_k_ff_1_q));  // open: Qn, preset, en, reset
  J_K_Flip_Flop j_k_ff_2 (
    .J(and_1_out), .clk(button_1_out), .K(and_1_out), .Q(j_k_ff_2_q));  // open: Qn, preset, en, reset
  not not_1 (not_1_out, j_k_ff_1_q);
  not not_2 (not_2_out, j_k_ff_2_q);
  and and_2 (and_2_out, not_1_out, not_2_out);
  and and_3 (and_3_out, j_k_ff_1_q, not_2_out);
  and and_4 (and_4_out, not_1_out, j_k_ff_2_q);
  and and_5 (and_5_out, j_k_ff_1_q, j_k_ff_2_q);
  or or_1 (or_1_out, and_2_out, and_3_out, and_4_out, and_5_out);
  or or_2 (or_2_out, and_3_out, and_4_out);
  or or_3 (or_3_out, and_3_out, and_4_out, and_5_out);
  or or_4 (or_4_out, and_3_out, and_4_out);
  or or_5 (or_5_out, and_2_out, and_4_out, and_5_out);
  _7_Segment_Display u_7_segment_display_1 (
    .g(or_3_out), .f(and_5_out), .a(or_2_out), .b(or_1_out), .e(and_3_out), .d(or_4_out), .c(or_5_out));  // open: dp
endmodule

module Counter (
  input  in_1,
  output out_2,
  output out_3,
  output out_4,
  output out_5
);

  wire and_1_out, and_2_out, and_3_out;

  and and_1 (and_1_out, 1'b1, out_2);
  and and_2 (and_2_out, and_1_out, out_3);
  and and_3 (and_3_out, and_2_out, out_4);
  J_K_Flip_Flop j_k_ff_1 (.J(1'b1), .clk(in_1), .K(1'b1), .Q(out_2));  // open: Qn, preset, en, reset
  J_K_Flip_Flop j_k_ff_2 (.J(and_1_out), .clk(in_1), .Q(out_3));  // open: K, Qn, preset, en, reset
  J_K_Flip_Flop j_k_ff_3 (.J(and_2_out), .clk(in_1), .Q(out_4));  // open: K, Qn, preset, en, reset
  J_K_Flip_Flop j_k_ff_4 (.J(and_3_out), .clk(in_1), .K(and_3_out), .Q(out_5));  // open: Qn, preset, en, reset
endmodule
