// Logisim project Proj 1.circ as structural Verilog: 2 circuits, main circuit main
module main (
  input  X0,
  input  X1,
  input  X2,
  input  C_in,
  input  Y0,
  input  Y1,
  input  Y2,
  output Sum1,
  output Sum2,
  output Sum3,
  output C_out
);

  wire full_adder_1_c_out, full_adder_2_c_out;

  Full_Adder full_adder_1 (.X(X0), .Y(Y0), .C_in(C_in), .Sum(Sum1), .C_out(full_adder_1_c_out));
  Full_Adder full_adder_2 (.X(X1), .Y(Y1), .C_in(full_adder_1_c_out), .Sum(Sum2), .C_out(full_adder_2_c_out));
  Full_Adder full_adder_3 (.X(X2), .Y(Y2), .C_in(full_adder_2_c_out), .Sum(Sum3), .C_out(C_out));
  LED led_1 (.in(Sum1));
  LED led_2 (.in(Sum2));
  LED led_3 (.in(Sum3));
endmodule

module Full_Adder (
  input  X,
  input  Y,
  input  C_in,
  output Sum,
  output C_out
);

  wire and_1_out, and_2_out, and_3_out, and_4_out, and_5_out, and_6_out, and_7_out, not_1_out, not_2_out,
       not_3_out;

  not not_1 (not_1_out, X);
  not not_2 (not_2_out, Y);
  not not_3 (not_3_out, C_in);
  and and_1 (and_1_out, not_1_out, not_2_out, C_in);
  and and_2 (and_2_out, not_1_out, Y, not_3_out);
  and and_3 (and_3_out, X, not_2_out, not_3_out);
  and and_4 (and_4_out, X, Y, C_in);
  and and_5 (and_5_out, Y, C_in);
  and and_6 (and_6_out, C_in, X);
  and and_7 (and_7_out, X, Y);
  or or_1 (C_out, and_5_out, and_6_out, and_7_out);
  or or_2 (Sum, and_1_out, and_2_out, and_3_out, and_4_out);
endmodule
