// Logisim project Proj2.circ as structural Verilog: 3 circuits, main circuit main
module main (
);

  wire bcd_1_out_5, bcd_1_out_6, bcd_1_out_7, bcd_1_out_8, bcd_1_out_9, bcd_1_out_10, bcd_1_out_11,
       clock_1_out, counter_1_out_2, counter_1_out_3, counter_1_out_4, counter_1_out_5;

  Counter counter_1 (
    .in_1(clock_1_out), .out_2(counter_1_out_2), .out_3(counter_1_out_3), .out_4(counter_1_out_4),
    .out_5(counter_1_out_5));
  Clock clock_1 (.out(clock_1_out));
  BCD bcd_1 (
    .A(counter_1_out_2), .B(counter_1_out_3), .C(counter_1_out_4), .D(counter_1_out_5), .out_5(bcd_1_out_5),
    .out_6(bcd_1_out_6), .out_7(bcd_1_out_7), .out_8(bcd_1_out_8), .out_9(bcd_1_out_9),
    .out_10(bcd_1_out_10), .out_11(bcd_1_out_11));
  _7_Segment_Display u_7_segment_display_1 (
    .g(bcd_1_out_11), .f(bcd_1_out_10), .a(bcd_1_out_5), .b(bcd_1_out_6), .e(bcd_1_out_9), .d(bcd_1_out_8),
    .c(bcd_1_out_7));  // open: dp
endmodule

module BCD (
  input  A,
  input  B,
  input  C,
  input  D,
  output out_5,
  output out_6,
  output out_7,
  output out_8,
  output out_9,
  output out_10,
  output out_11
);

  wire and_1_out, and_2_out, and_3_out, and_4_out, and_5_out, and_6_out, and_7_out, and_8_out, and_9_out,
       and_10_out, and_11_out, and_12_out, and_13_out, and_14_out, and_15_out, and_16_out, and_17_out,
       not_1_out, not_2_out, not_3_out, not_4_out;

  not not_1 (not_1_out, A);
  not not_2 (not_2_out, B);
  not not_3 (not_3_out, C);
  not not_4 (not_4_out, D);
  and and_1 (and_1_out, not_1_out, not_3_out);
  and and_2 (and_2_out, A, C);
  and and_3 (and_3_out, not_1_out, not_2_out);
  and and_4 (and_4_out, A, B);
  and and_5 (and_5_out, A, not_4_out);
  and and_6 (and_6_out, not_1_out, not_3_out);
  and and_7 (and_7_out, not_1_out, B);
  and and_8 (and_8_out, B, not_3_out);
  and and_9 (and_9_out, A, C, not_2_out);
  and and_10 (and_10_out, not_1_out, not_3_out);
  and and_11 (and_11_out, not_1_out, B);
  and and_12 (and_12_out, not_1_out, not_2_out);
  and and_13 (and_13_out, not_1_out, C);
  and and_14 (and_14_out, not_2_out, C);
  and and_15 (and_15_out, not_2_out, C);
  and and_16 (and_16_out, not_1_out, B);
  and and_17 (and_17_out, B, not_3_out);
  or or_1 (out_5, and_1_out, D, B, and_2_out);
  or or_2 (out_6, and_3_out, not_3_out, and_4_out);
  or or_3 (out_7, and_5_out, C, not_2_out);
  or or_4 (out_9, and_10_out, and_11_out);
  or or_5 (out_8, and_6_out, D, and_7_out, and_8_out, and_9_out);
  or or_6 (out_10, and_12_out, D, and_13_out, and_14_out);
  or or_7 (out_11, D, and_15_out, and_16_out, and_17_out);
endmodule

module Counter (
  input  in_1,
  output out_2,
  output out_3,
  output out_4,
  output out_5
);

  wire and_1_out, j_k_ff_1_qn, j_k_ff_2_qn, j_k_ff_3_qn;

  J_K_Flip_Flop j_k_ff_1 (
    .J(1'b1), .clk(in_1), .K(1'b1), .Q(out_2), .Qn(j_k_ff_1_qn), .en(1'b1), .reset(and_1_out));  // open: preset
  J_K_Flip_Flop j_k_ff_2 (
    .J(1'b1), .clk(j_k_ff_1_qn), .K(1'b1), .Q(out_3), .Qn(j_k_ff_2_qn), .en(1'b1), .reset(and_1_out));  // open: preset
  J_K_Flip_Flop j_k_ff_3 (
    .J(1'b1), .clk(j_k_ff_2_qn), .K(1'b1), .Q(out_4), .Qn(j_k_ff_3_qn), .en(1'b1), .reset(and_1_out));  // open: preset
  J_K_Flip_Flop j_k_ff_4 (.J(1'b1), .clk(j_k_ff_3_qn), .K(1'b1), .Q(out_5), .reset(and_1_out));  // open: Qn, preset, en
  and and_1 (and_1_out, out_3, out_5);
endmodule
